// Logisim project s-mips.circ as structural Verilog
module S_MIPS_Board (
  input  DESHABILITAR_DISPATCHER,
  output halt
);

  wire button_1_out, CLK, CS, d_ff_1_q, LCLR, LoadRAM, LoadRAMOn, LW, R_R_W, R_W, ram_dispatcher_1_finished,
       RCS, Reset_out, RST, TTY_EN;
  wire [2:0] KDB;
  wire [3:0] LMask, Mask, ram_1_read_time, ram_1_write_time, RMask;
  wire [6:0] KDB_DATA, TTY_DATA;
  wire [15:0] Addr, LAddr, RAddr;
  wire [31:0] I0, I1, I2, I3, LData, ram_1_data_out_0, ram_1_data_out_1, ram_1_data_out_2, ram_1_data_out_3,
       RI0, RI1, RI2, RI3;

  TTY #(.rows(25), .cols(80)) tty_1 (.data(TTY_DATA), .clk(CLK), .we(TTY_EN), .clr(RST));
  not not_1 (LoadRAMOn, ram_dispatcher_1_finished);
  RAM_Dispatcher ram_dispatcher_1 (
    .WriteTime(ram_1_write_time), .Clock(CLK), .Data(LData), .Address(LAddr), .Mask(LMask),
    .Finished(ram_dispatcher_1_finished), .Write(LW), .CLR(LCLR));
  Keyboard #(.buflen(64)) keyboard_1 (.clk(CLK), .re(KDB[0]), .avail(KDB[2]), .data(KDB_DATA));  // open: clr
  RAM ram_1 (
    .Address(RAddr), .Data_Out_0(ram_1_data_out_0), .Data_Out_1(ram_1_data_out_1),
    .Data_Out_2(ram_1_data_out_2), .Data_Out_3(ram_1_data_out_3), .Data_In_0(RI0), .Data_In_1(RI1),
    .Data_In_2(RI2), .Data_In_3(RI3), .Mask(RMask), .nRead_Write(R_R_W), .Chip_Select(RCS),
    .Read_Time(ram_1_read_time), .Reset(button_1_out), .Write_Time(ram_1_write_time));
  Button button_1 (.out(button_1_out));
  D_Flip_Flop d_ff_1 (.clk(CLK), .D(1'b1), .Q(d_ff_1_q), .reset(Reset_out));  // open: Qn, preset, en
  Button Reset (.out(Reset_out));
  S_MIPS s_mips_1 (
    .RAM_Out_0(ram_1_data_out_0), .RAM_In_0(I0), .RAM_Out_1(ram_1_data_out_1), .RAM_In_1(I1),
    .RAM_Out_2(ram_1_data_out_2), .RAM_In_2(I2), .RAM_Out_3(ram_1_data_out_3), .RAM_In_3(I3), .Mask(Mask),
    .Read_Time(ram_1_read_time), .Write_Time(ram_1_write_time), .Address(Addr), .Kbd_Available(KDB[2]),
    .TTY_Enable(TTY_EN), .Kbd_ASCII_Data(KDB_DATA), .TTY_ASCII_Data(TTY_DATA), .Reset(RST),
    .nRead_Write(R_W), .Clock(CLK), .Chip_Select(CS), .Kbd_Enable(KDB[0]), .Kbd_Clear(KDB[1]), .Stop(halt));
  D_Flip_Flop d_ff_2 (.clk(CLK), .D(d_ff_1_q), .Qn(LCLR), .reset(Reset_out));  // open: Q, preset, en
  or or_1 (RST, LCLR, LoadRAM);
  Clock clock_1 (.out(CLK));
  Multiplexer #(.width(32), .enable("false")) multiplexer_1 (.in0(I0), .in1(LData), .out(RI0), .sel(LoadRAM));
  Multiplexer #(.width(32), .enable("false")) multiplexer_2 (.in0(I1), .in1(LData), .out(RI1), .sel(LoadRAM));
  Multiplexer #(.width(32), .enable("false")) multiplexer_3 (.in0(I2), .in1(LData), .out(RI2), .sel(LoadRAM));
  Multiplexer #(.width(32), .enable("false")) multiplexer_4 (.in0(I3), .in1(LData), .out(RI3), .sel(LoadRAM));
  and and_1 (LoadRAM, ~DESHABILITAR_DISPATCHER, LoadRAMOn);  // AND_Gate
  Multiplexer #(.width(16), .enable("false")) multiplexer_5 (.in0(Addr), .in1(LAddr), .out(RAddr), .sel(LoadRAM));
  Multiplexer #(.width(4), .enable("false")) multiplexer_6 (.in0(Mask), .in1(LMask), .out(RMask), .sel(LoadRAM));
  Multiplexer #(.enable("false")) multiplexer_7 (.in0(CS), .in1(LW), .out(RCS), .sel(LoadRAM));
  Multiplexer #(.enable("false")) multiplexer_8 (.in0(R_W), .in1(LW), .out(R_R_W), .sel(LoadRAM));

  // Notes on the sheet:
  //   NO MODIFICAR
  //   Keyboard
endmodule

module RAM (
  input  [15:0] Address,
  input  [31:0] Data_In_0,
  input  [31:0] Data_In_1,
  input  [31:0] Data_In_2,
  input  [31:0] Data_In_3,
  input  [3:0] Mask,
  input  nRead_Write,
  input  Chip_Select,
  input  Reset,
  output [31:0] Data_Out_0,
  output [31:0] Data_Out_1,
  output [31:0] Data_Out_2,
  output [31:0] Data_Out_3,
  output [3:0] Read_Time,
  output [3:0] Write_Time
);

  wire and_2_out, and_3_out, and_4_out, and_5_out, and_6_out, and_7_out, and_8_out, and_9_out, Changed, CLK,
       comparator_2_eq, comparator_3_eq, comparator_4_eq, comparator_5_eq, comparator_6_eq, Count,
       demultiplexer_3_out0, Idle, Idle_q, Load, Load0, Load1, nand_1_out, or_1_out, or_2_out, or_3_out,
       or_4_out, or_5_out, or_6_out, or_7_out, or_8_out, or_9_out, or_10_out, Proc_q, Update_Mem, Zero_Time;
  wire [3:0] counter_1_q, multiplexer_1_out, subtractor_1_out;
  wire [31:0] register_1_q, register_2_q, register_3_q, register_4_q, register_5_q;

  // Probe on 4'b0011
  // Probe on 4'b0010
  Multiplexer #(.width(4), .enable("false")) multiplexer_1 (
    .in0(4'b0011), .in1(4'b0010), .out(multiplexer_1_out), .sel(nRead_Write));
  or or_1 (or_1_out, Idle, Update_Mem);
  or or_2 (or_2_out, ~Chip_Select, Reset);  // OR_Gate
  Subtractor #(.width(4)) subtractor_1 (.a(multiplexer_1_out), .b(4'b0010), .out(subtractor_1_out));  // open: bin, bout
  Demultiplexer #(.enable("false")) demultiplexer_1 (.out0(Idle), .out1(Load0), .in(Idle_q), .sel(Changed));
  D_Flip_Flop u_Idle (.clk(CLK), .D(or_1_out), .Q(Idle_q), .preset(or_2_out));  // open: Qn, en, reset
  // Probe on counter_1_q
  Counter #(.width(4), .max('hf)) counter_1 (
    .load(Load), .D(subtractor_1_out), .count(Count), .Q(counter_1_q), .clk(CLK), .clr(or_3_out));  // open: carry
  or or_3 (or_3_out, ~Chip_Select, Reset);  // OR_Gate
  Comparator #(.width(4), .mode("unsigned")) comparator_1 (
    .a(4'b0000), .b(counter_1_q), .eq(Zero_Time));  // open: gt, lt
  or or_4 (or_4_out, Count, Load0, Load1);
  Register_part #(.width(32)) register_1 (.D(Data_In_0), .en(Chip_Select), .Q(register_1_q), .clk(CLK), .clr(or_5_out));
  or or_5 (or_5_out, ~Chip_Select, Reset);  // OR_Gate
  Register_part #(.width(32)) register_2 (.D(Data_In_1), .en(Chip_Select), .Q(register_2_q), .clk(CLK), .clr(or_6_out));
  or or_6 (or_6_out, ~Chip_Select, Reset);  // OR_Gate
  Register_part #(.width(32)) register_3 (.D(Data_In_2), .en(Chip_Select), .Q(register_3_q), .clk(CLK), .clr(or_7_out));
  or or_7 (or_7_out, ~Chip_Select, Reset);  // OR_Gate
  Register_part #(.width(32)) register_4 (.D(Data_In_3), .en(Chip_Select), .Q(register_4_q), .clk(CLK), .clr(or_8_out));
  or or_8 (or_8_out, ~Chip_Select, Reset);  // OR_Gate
  Register_part #(.width(32)) register_5 (
    .D({{11{1'b1}}, nRead_Write, Mask, Address}), .en(Chip_Select), .Q(register_5_q), .clk(CLK),
    .clr(or_9_out));
  or or_9 (or_9_out, ~Chip_Select, Reset);  // OR_Gate
  D_Flip_Flop Proc (.clk(CLK), .D(or_4_out), .Q(Proc_q), .reset(or_10_out));  // open: Qn, preset, en
  or or_10 (or_10_out, ~Chip_Select, Reset);  // OR_Gate
  Demultiplexer #(.enable("false")) demultiplexer_2 (
    .out0(Count), .out1(Update_Mem), .in(demultiplexer_3_out0), .sel(Zero_Time));
  Demultiplexer #(.enable("false")) demultiplexer_3 (
    .out0(demultiplexer_3_out0), .out1(Load1), .in(Proc_q), .sel(Changed));
  Clock clock_1 (.out(CLK));
  Comparator #(.width(32)) comparator_2 (.a(register_1_q), .b(Data_In_0), .eq(comparator_2_eq));  // open: gt, lt
  Comparator #(.width(32)) comparator_3 (.a(register_2_q), .b(Data_In_1), .eq(comparator_3_eq));  // open: gt, lt
  Comparator #(.width(32)) comparator_4 (.a(register_3_q), .b(Data_In_2), .eq(comparator_4_eq));  // open: gt, lt
  Comparator #(.width(32)) comparator_5 (.a(register_4_q), .b(Data_In_3), .eq(comparator_5_eq));  // open: gt, lt
  Comparator #(.width(32)) comparator_6 (
    .a(register_5_q), .b({{11{1'b1}}, nRead_Write, Mask, Address}), .eq(comparator_6_eq));  // open: gt, lt
  nand nand_1 (nand_1_out, comparator_6_eq, comparator_2_eq, comparator_3_eq, comparator_4_eq, comparator_5_eq);
  and and_1 (Changed, nand_1_out, Chip_Select);
  or or_11 (Load, Count, Load1, Load0);
  and and_2 (and_2_out, Mask[0], Update_Mem, nRead_Write);
  and and_3 (and_3_out, Mask[1], Update_Mem, nRead_Write);
  and and_4 (and_4_out, Mask[2], Update_Mem, nRead_Write);
  and and_5 (and_5_out, Mask[3], Update_Mem, nRead_Write);
  RAM_part #(.addrWidth(16), .dataWidth(32), .bus("separate")) ram_1 (
    .addr(Address), .din(Data_In_0), .data(Data_Out_0), .str(and_2_out), .sel(Chip_Select), .clk(CLK),
    .ld(and_6_out), .clr(Reset));
  and and_6 (and_6_out, ~nRead_Write, Idle);  // AND_Gate
  RAM_part #(.addrWidth(16), .dataWidth(32), .bus("separate")) ram_2 (
    .addr(Address), .din(Data_In_1), .data(Data_Out_1), .str(and_3_out), .sel(Chip_Select), .clk(CLK),
    .ld(and_7_out), .clr(Reset));
  and and_7 (and_7_out, ~nRead_Write, Idle);  // AND_Gate
  RAM_part #(.addrWidth(16), .dataWidth(32), .bus("separate")) ram_3 (
    .addr(Address), .din(Data_In_2), .data(Data_Out_2), .str(and_4_out), .sel(Chip_Select), .clk(CLK),
    .ld(and_8_out), .clr(Reset));
  and and_8 (and_8_out, ~nRead_Write, Idle);  // AND_Gate
  RAM_part #(.addrWidth(16), .dataWidth(32), .bus("separate")) ram_4 (
    .addr(Address), .din(Data_In_3), .data(Data_Out_3), .str(and_5_out), .sel(Chip_Select), .clk(CLK),
    .ld(and_9_out), .clr(Reset));
  and and_9 (and_9_out, ~nRead_Write, Idle);  // AND_Gate

  assign Read_Time = 4'b0011;
  assign Write_Time = 4'b0010;

  // Other names for the same wires on the sheet: M0 = Mask[0]; M1 = Mask[1]; M2 = Mask[2]; M3 = Mask[3];
  //   RW = nRead_Write; CLR = Reset; CS = Chip_Select; Load2 = Count

  // Notes on the sheet:
  //   NO MODIFICAR
  //   excepto quizás los valores RT y WT
  //   BANK0
  //   BANK1
  //   BANK2
  //   BANK3
endmodule

module S_MIPS (
  input  [31:0] RAM_Out_0,
  input  [31:0] RAM_Out_1,
  input  [31:0] RAM_Out_2,
  input  [31:0] RAM_Out_3,
  input  [3:0] Read_Time,
  input  [3:0] Write_Time,
  input  Kbd_Available,
  input  [6:0] Kbd_ASCII_Data,
  input  Reset,
  input  Clock,
  output [31:0] RAM_In_0,
  output [31:0] RAM_In_1,
  output [31:0] RAM_In_2,
  output [31:0] RAM_In_3,
  output [3:0] Mask,
  output [15:0] Address,
  output TTY_Enable,
  output [6:0] TTY_ASCII_Data,
  output nRead_Write,
  output Chip_Select,
  output Kbd_Enable,
  output Kbd_Clear,
  output Stop
);

  wire controlunit_1_out_6, controlunit_1_out_8, controlunit_1_out_12, controlunit_1_out_13,
       controlunit_1_out_14, controlunit_1_out_15, controlunit_1_out_20, controlunit_1_out_23, RAM_Ready,
       RI_Start, RI_Write;
  wire [1:0] Bank, controlunit_1_out_11, controlunit_1_out_16, controlunit_1_out_21;
  wire [2:0] controlunit_1_out_7, controlunit_1_out_9, controlunit_1_out_18;
  wire [5:0] FuncCode, OpCode;
  wire [31:0] Address_t, RAM_Data, swaplittleendian_1_output, To_RAM;

  ControlUnit_2 controlunit_1 (
    .in_1(OpCode), .in_2(FuncCode), .in_3(Clock), .in_4(Reset), .in_5(RAM_Ready), .out_24(Stop),
    .out_13(controlunit_1_out_13), .out_16(controlunit_1_out_16), .out_21(controlunit_1_out_21),
    .out_7(controlunit_1_out_7), .out_18(controlunit_1_out_18), .out_14(controlunit_1_out_14),
    .out_20(controlunit_1_out_20), .out_11(controlunit_1_out_11), .out_9(controlunit_1_out_9),
    .out_6(controlunit_1_out_6), .out_10(RI_Write), .out_19(RI_Start), .out_22(Kbd_Enable),
    .out_17(TTY_Enable), .out_8(controlunit_1_out_8), .out_23(controlunit_1_out_23),
    .out_15(controlunit_1_out_15), .out_12(controlunit_1_out_12));
  RamHandler ramhandler_1 (
    .Addres_In(Address_t), .Ram_out_0(RAM_Out_0), .Ram_out_1(RAM_Out_1), .Ram_out_2(RAM_Out_2),
    .Ram_out_3(RAM_Out_3), .Read_Time(Read_Time), .Clk(Clock), .Rst(Reset), .Write_Time(Write_Time),
    .Start(RI_Start), .R_W(RI_Write), .From_RAM(RAM_Data), .Mask(Mask), .ADDR(Address), .Bank(Bank),
    .RAMReady(RAM_Ready), .Chip_Select(Chip_Select), .RAM_Write(nRead_Write));
  DataPath_2 datapath_1 (
    .RAM_out(RAM_Data), .DAS(controlunit_1_out_20), .DOS(controlunit_1_out_14), .AS(controlunit_1_out_13),
    .BS(controlunit_1_out_16), .BCS(controlunit_1_out_21), .AddrS(controlunit_1_out_11),
    .DIS(controlunit_1_out_9), .ALUS(controlunit_1_out_7), .FlagS(controlunit_1_out_18),
    .IM_R_W(controlunit_1_out_12), .PC_R_W(controlunit_1_out_15), .LH_R_W(controlunit_1_out_6),
    .RF_R_W(controlunit_1_out_8), .KBD_Data(Kbd_ASCII_Data), .SP_R_W(controlunit_1_out_23),
    .Address(Address_t), .Data_Out(To_RAM), .OpCode(OpCode), .FuncCode(FuncCode), .tty_out(TTY_ASCII_Data),
    .Clk(Clock), .RST(Reset), .KBD_Avail(Kbd_Available));
  SwapLittleEndian swaplittleendian_1 (.Input(To_RAM), .Output(swaplittleendian_1_output));
  Demultiplexer #(.select(2), .width(32), .enable("false")) demultiplexer_1 (
    .out0(RAM_In_0), .out1(RAM_In_1), .out2(RAM_In_2), .out3(RAM_In_3), .in(swaplittleendian_1_output),
    .sel(Bank));

  assign Kbd_Clear = Reset;

  // Other names for the same wires on the sheet: CLK = Clock; CS = Chip_Select; KBD_AVAIL = Kbd_Available;
  //   KBD_DATA[6:0] = Kbd_ASCII_Data; RAM_A[15:0] = Address; RAM_MASK[3:0] = Mask; RAM_OUTPUT_0[31:0] = RAM_Out_0;
  //   RAM_OUTPUT_1[31:0] = RAM_Out_1; RAM_OUTPUT_2[31:0] = RAM_Out_2; RAM_OUTPUT_3[31:0] = RAM_Out_3; RST = Reset;
  //   RW = nRead_Write; TTY_DATA[6:0] = TTY_ASCII_Data; TTY_EN = TTY_Enable

  // Notes on the sheet:
  //   RAM TIMING
  //   KEYBOARD
  //   SEQUENCING
  //   DATA FROM RAM
  //   RAM ADDRESS
  //   TTY
  //   RAM CONTROL
  //   KEYBOARD
  //   DATA TO RAM
  //   DATA WRITE MASK
endmodule

module RAM_Dispatcher (
  input  [3:0] WriteTime,
  input  Clock,
  input  CLR,
  output [31:0] Data,
  output [15:0] Address,
  output [3:0] Mask,
  output Finished,
  output Write
);

  wire demultiplexer_2_out1, demultiplexer_3_out1, End, IDLE_q, IncAddr, Load, or_1_out, or_2_out, While_q,
       WriteEnd;
  wire [3:0] counter_1_q;
  wire [31:0] CurrentAddress_q;

  Counter #(.width(32), .max('hffffffff)) CurrentAddress (
    .count(IncAddr), .Q({CurrentAddress_q[31:18], Address, CurrentAddress_q[1:0]}), .clk(Clock), .clr(CLR));  // open: load, D, carry
  or or_1 (or_1_out, IncAddr, demultiplexer_3_out1, Finished);
  D_Flip_Flop IDLE (.clk(Clock), .D(or_1_out), .Q(IDLE_q), .preset(CLR));  // open: Qn, en, reset
  Demultiplexer #(.enable("false")) demultiplexer_1 (.out0(Load), .out1(Finished), .in(IDLE_q), .sel(End));
  D_Flip_Flop While (.clk(Clock), .D(or_2_out), .Q(While_q), .reset(CLR));  // open: Qn, preset, en
  or or_2 (or_2_out, Write, Load);
  RAM_part #(.addrWidth(18), .dataWidth(32)) ram_1 (
    .addr({Address, CurrentAddress_q[1:0]}), .data(Data), .clk(Clock));  // open: sel, ld, clr
  Demultiplexer #(.enable("false")) demultiplexer_2 (
    .out0(Write), .out1(demultiplexer_2_out1), .in(While_q), .sel(WriteEnd));
  Decoder #(.select(2)) decoder_1 (
    .out0(Mask[0]), .out1(Mask[1]), .out2(Mask[2]), .out3(Mask[3]), .sel(CurrentAddress_q[1:0]));  // open: en
  Demultiplexer #(.enable("false")) demultiplexer_3 (
    .out0(IncAddr), .out1(demultiplexer_3_out1), .in(demultiplexer_2_out1), .sel(End));
  Counter #(.width(4), .max('hf)) counter_1 (
    .load(Load), .D(WriteTime), .count(Write), .Q(counter_1_q), .clk(Clock));  // open: carry, clr
  Comparator #(.width(32)) comparator_1 (.a(Data), .b({32{1'b1}}), .eq(End));  // open: gt, lt
  Comparator #(.width(4)) comparator_2 (.a(4'b0000), .b(counter_1_q), .eq(WriteEnd));  // open: gt, lt

  // Other names for the same wires on the sheet: CLK = Clock; Count = Write; WT[3:0] = WriteTime
endmodule

module DataPath_2 (
  input  [31:0] RAM_out,
  input  DAS,
  input  DOS,
  input  AS,
  input  [1:0] BS,
  input  [1:0] BCS,
  input  [1:0] AddrS,
  input  [2:0] DIS,
  input  [2:0] ALUS,
  input  [2:0] FlagS,
  input  IM_R_W,
  input  PC_R_W,
  input  LH_R_W,
  input  RF_R_W,
  input  [6:0] KBD_Data,
  input  SP_R_W,
  input  KBD_Avail,
  input  Clk,
  input  RST,
  output [31:0] Address,
  output [31:0] Data_Out,
  output [5:0] OpCode,
  output [5:0] FuncCode,
  output [6:0] tty_out
);

  wire N, P, Z;
  wire [4:0] DA, RD, RS, RT;
  wire [25:0] Dest;
  wire [31:0] bit_extender_1_out, branchcontrol_1_pc_out, Hi, HiI, K, kbd, Lo, LoI, multiplexer_1_out,
       multiplexer_4_out, multiplexer_5_out, PC, R, rnd, RT_t, SP, UK;
  wire [31:7] RS_t;

  InstructionSplitter instructionsplitter_1 (
    .Inst(RAM_out), .IM_R_W(IM_R_W), .Clk(Clk), .Rst(RST), .Op(OpCode), .Func__Code(FuncCode),
    .Destino(Dest), .RS(RS), .RT(RT), .RD(RD), .Sign_Const(K), .Unsgn_Const(UK));
  Multiplexer #(.select(3), .width(32), .enable("false")) multiplexer_1 (
    .in0(R), .in1(RAM_out), .in3(Lo), .in5(Hi), .in6(rnd), .in7(kbd), .out(multiplexer_1_out), .sel(DIS));  // open: in2, in4
  Multiplexer #(.width(5), .enable("false")) multiplexer_2 (.in0(RD), .in1(RT), .out(DA), .sel(DAS));
  assign bit_extender_1_out = {{25{1'b0}}, KBD_Data};  // Bit_Extender bit_extender_1
  RegisterFile registerfile_1 (
    .DA(DA), .DI(multiplexer_1_out), .R_W(RF_R_W), .SA(RS), .SB(RT), .Clk(Clk), .Reset(RST), .Lo(LoI),
    .Hi(HiI), .LH_RW(LH_R_W), .SP(R), .SP_RW(SP_R_W), .Data_A({RS_t, tty_out}), .Stack_Pointer(SP),
    .Data_B(RT_t), .Lo_2(Lo), .Hi_2(Hi));
  Multiplexer #(.width(32), .enable("false")) multiplexer_3 (
    .in0(bit_extender_1_out), .in1({32{1'b1}}), .out(kbd), .sel(KBD_Avail));
  BranchControl branchcontrol_1 (
    .PC_in(PC), .BCSel(BCS), .FlagS(FlagS), .K(K), .Destino(Dest), .Register({RS_t, tty_out}),
    .PC_out(branchcontrol_1_pc_out), .Z(Z), .N(N), .P(P));
  Multiplexer #(.width(32), .enable("false")) multiplexer_4 (
    .in0({RS_t, tty_out}), .in1(SP), .out(multiplexer_4_out), .sel(AS));
  Multiplexer #(.select(2), .width(32), .enable("false")) multiplexer_5 (
    .in0(RT_t), .in1(K), .in2(UK), .in3(32'h4), .out(multiplexer_5_out), .sel(BS));
  Random #(.width(32)) random_1 (.clk(Clk), .out(rnd));  // open: next, clr
  Register register_1 (.Data_In(branchcontrol_1_pc_out), .Load(PC_R_W), .Clock(Clk), .Reset(RST), .Current_Value(PC));
  ALU alu_1 (
    .A(multiplexer_4_out), .B(multiplexer_5_out), .S(ALUS), .R(R), .Positive(P), .Zero(Z), .Negative(N),
    .Lo(LoI), .Hi(HiI));
  Multiplexer #(.select(2), .width(32), .enable("false")) multiplexer_6 (
    .in0(PC), .in1(R), .in2(SP), .out(Address), .sel(AddrS));  // open: in3
  Multiplexer #(.width(32), .enable("false")) multiplexer_7 (
    .in0(RT_t), .in1({RS_t, tty_out}), .out(Data_Out), .sel(DOS));

  // Other names for the same wires on the sheet: Func[5:0] = FuncCode; IM_RW = IM_R_W; LH_RW = LH_R_W;
  //   OP[5:0] = OpCode; PC_RW = PC_R_W; RAM[31:0] = RAM_out; RF_RW = RF_R_W; RS_t[6:0] = tty_out; SP_RW = SP_R_W

  // Notes on the sheet:
  //   Selectors
  //   Loads
  //   Data Path
  //   PC
endmodule

module Register (
  input  [31:0] Data_In,
  input  Load,
  input  Clock,
  input  Reset,
  output [31:0] Current_Value
);

  Register_part #(.width(32), .trigger("falling")) register_1 (
    .D(Data_In), .en(Load), .Q(Current_Value), .clk(Clock), .clr(Reset));
  // Probe on Current_Value

  // Notes on the sheet:
  //   Register 32 bits
endmodule

module RegisterFile (
  input  [4:0] DA,
  input  [31:0] DI,
  input  R_W,
  input  [4:0] SA,
  input  [4:0] SB,
  input  Clk,
  input  Reset,
  input  [31:0] Lo,
  input  [31:0] Hi,
  input  LH_RW,
  input  [31:0] SP,
  input  SP_RW,
  output [31:0] Data_A,
  output [31:0] Stack_Pointer,
  output [31:0] Data_B,
  output [31:0] Lo_2,
  output [31:0] Hi_2
);

  wire L1, L2, L3, L4, L5, L6, L7, L8, L9, L10, L11, L12, L13, L14, L15, L16, L17, L18, L19, L20, L21, L22,
       L23, L24, L25, L26, L27, L28, L29, L30, L31, SPW;
  wire [31:0] R1, R2, R3, R4, R5, R6, R7, R8, R9, R10, R11, R12, R13, R14, R15, R16, R17, R18, R19, R20, R21,
       R22, R23, R24, R25, R26, R27, R28, R29, R30;

  Decoder #(.select(5), .disabled(0)) decoder_1 (
    .out1(L1), .out2(L2), .out3(L3), .out4(L4), .out5(L5), .out6(L6), .out7(L7), .out8(L8), .out9(L9),
    .out10(L10), .out11(L11), .out12(L12), .out13(L13), .out14(L14), .out15(L15), .out16(L16), .out17(L17),
    .out18(L18), .out19(L19), .out20(L20), .out21(L21), .out22(L22), .out23(L23), .out24(L24), .out25(L25),
    .out26(L26), .out27(L27), .out28(L28), .out29(L29), .out30(L30), .out31(L31), .sel(DA), .en(R_W));  // open: out0
  Register register_1 (.Data_In(Lo), .Load(LH_RW), .Clock(Clk), .Reset(Reset), .Current_Value(Lo_2));
  Register register_2 (.Data_In(Hi), .Load(LH_RW), .Clock(Clk), .Reset(Reset), .Current_Value(Hi_2));
  or or_1 (SPW, SP_RW, L31);
  Register register_3 (.Data_In(DI), .Load(L1), .Clock(Clk), .Reset(Reset), .Current_Value(R1));
  Register register_4 (.Data_In(DI), .Load(L2), .Clock(Clk), .Reset(Reset), .Current_Value(R2));
  Register register_5 (.Data_In(DI), .Load(L3), .Clock(Clk), .Reset(Reset), .Current_Value(R3));
  Register register_6 (.Data_In(DI), .Load(L4), .Clock(Clk), .Reset(Reset), .Current_Value(R4));
  Register register_7 (.Data_In(DI), .Load(L5), .Clock(Clk), .Reset(Reset), .Current_Value(R5));
  Register register_8 (.Data_In(DI), .Load(L6), .Clock(Clk), .Reset(Reset), .Current_Value(R6));
  Register register_9 (.Data_In(DI), .Load(L7), .Clock(Clk), .Reset(Reset), .Current_Value(R7));
  Register register_10 (.Data_In(DI), .Load(L8), .Clock(Clk), .Reset(Reset), .Current_Value(R8));
  Register register_11 (.Data_In(DI), .Load(L9), .Clock(Clk), .Reset(Reset), .Current_Value(R9));
  Register register_12 (.Data_In(DI), .Load(L10), .Clock(Clk), .Reset(Reset), .Current_Value(R10));
  Register register_13 (.Data_In(DI), .Load(L11), .Clock(Clk), .Reset(Reset), .Current_Value(R11));
  Register register_14 (.Data_In(DI), .Load(L12), .Clock(Clk), .Reset(Reset), .Current_Value(R12));
  Register register_15 (.Data_In(DI), .Load(L13), .Clock(Clk), .Reset(Reset), .Current_Value(R13));
  Register register_16 (.Data_In(DI), .Load(L14), .Clock(Clk), .Reset(Reset), .Current_Value(R14));
  Register register_17 (.Data_In(DI), .Load(L15), .Clock(Clk), .Reset(Reset), .Current_Value(R15));
  Register register_18 (.Data_In(DI), .Load(L16), .Clock(Clk), .Reset(Reset), .Current_Value(R16));
  Register register_19 (.Data_In(DI), .Load(L17), .Clock(Clk), .Reset(Reset), .Current_Value(R17));
  Register register_20 (.Data_In(DI), .Load(L18), .Clock(Clk), .Reset(Reset), .Current_Value(R18));
  Register register_21 (.Data_In(DI), .Load(L19), .Clock(Clk), .Reset(Reset), .Current_Value(R19));
  Register register_22 (.Data_In(DI), .Load(L20), .Clock(Clk), .Reset(Reset), .Current_Value(R20));
  Register register_23 (.Data_In(DI), .Load(L21), .Clock(Clk), .Reset(Reset), .Current_Value(R21));
  Register register_24 (.Data_In(DI), .Load(L22), .Clock(Clk), .Reset(Reset), .Current_Value(R22));
  Register register_25 (.Data_In(DI), .Load(L23), .Clock(Clk), .Reset(Reset), .Current_Value(R23));
  Register register_26 (.Data_In(DI), .Load(L24), .Clock(Clk), .Reset(Reset), .Current_Value(R24));
  Register register_27 (.Data_In(DI), .Load(L25), .Clock(Clk), .Reset(Reset), .Current_Value(R25));
  Register register_28 (.Data_In(DI), .Load(L26), .Clock(Clk), .Reset(Reset), .Current_Value(R26));
  Register register_29 (.Data_In(DI), .Load(L27), .Clock(Clk), .Reset(Reset), .Current_Value(R27));
  Register register_30 (.Data_In(DI), .Load(L28), .Clock(Clk), .Reset(Reset), .Current_Value(R28));
  Register register_31 (.Data_In(DI), .Load(L29), .Clock(Clk), .Reset(Reset), .Current_Value(R29));
  Register register_32 (.Data_In(DI), .Load(L30), .Clock(Clk), .Reset(Reset), .Current_Value(R30));
  Register register_33 (.Data_In(SP), .Load(SPW), .Clock(Clk), .Reset(Reset), .Current_Value(Stack_Pointer));
  Multiplexer #(.select(5), .width(32), .enable("false")) multiplexer_1 (
    .in0({32{1'b0}}), .in1(R1), .in2(R2), .in3(R3), .in4(R4), .in5(R5), .in6(R6), .in7(R7), .in8(R8),
    .in9(R9), .in10(R10), .in11(R11), .in12(R12), .in13(R13), .in14(R14), .in15(R15), .in16(R16), .in17(R17),
    .in18(R18), .in19(R19), .in20(R20), .in21(R21), .in22(R22), .in23(R23), .in24(R24), .in25(R25),
    .in26(R26), .in27(R27), .in28(R28), .in29(R29), .in30(R30), .in31(Stack_Pointer), .out(Data_A), .sel(SA));
  Multiplexer #(.select(5), .width(32), .enable("false")) multiplexer_2 (
    .in0({32{1'b0}}), .in1(R1), .in2(R2), .in3(R3), .in4(R4), .in5(R5), .in6(R6), .in7(R7), .in8(R8),
    .in9(R9), .in10(R10), .in11(R11), .in12(R12), .in13(R13), .in14(R14), .in15(R15), .in16(R16), .in17(R17),
    .in18(R18), .in19(R19), .in20(R20), .in21(R21), .in22(R22), .in23(R23), .in24(R24), .in25(R25),
    .in26(R26), .in27(R27), .in28(R28), .in29(R29), .in30(R30), .in31(Stack_Pointer), .out(Data_B), .sel(SB));

  // Other names for the same wires on the sheet: Hi_t[31:0] = Hi_2; Lo_t[31:0] = Lo_2; LoHiRW = LH_RW; Rst = Reset;
  //   SP_t[31:0] = Stack_Pointer; SPIn[31:0] = SP

  // Notes on the sheet:
  //   Inputs
  //   Data Address
  //   Data In
  //   Read/Write
  //   Selector A
  //   Selector B
  //   Lo HIi R/W
  //   Lo
  //   Hi
  //   SP R/W
  //   SP
  //   Outputs
endmodule

module Sign (
  input  [31:0] In,
  output [31:0] Out,
  output Sign
);

  wire [31:0] negator_1_out;

  BitSelector #(.width(32)) bitselector_1 (.in(In), .out(Sign), .sel({5{1'b1}}));
  Multiplexer #(.width(32), .enable("false")) multiplexer_1 (.in0(In), .in1(negator_1_out), .out(Out), .sel(Sign));
  Negator #(.width(32)) negator_1 (.in(In), .out(negator_1_out));

  // Notes on the sheet:
  //   Absolute Value and Sign
endmodule

module SignDiv (
  input  [31:0] A,
  input  [31:0] B,
  output [31:0] Low,
  output [31:0] High
);

  wire Sign_A, Sign_B, Sign_Quo;
  wire [31:0] minus_Quo, minus_Rem, plus_Quo, plus_Rem, sign_1_out, sign_2_out;

  Sign sign_1 (.In(A), .Out(sign_1_out), .Sign(Sign_A));
  Sign sign_2 (.In(B), .Out(sign_2_out), .Sign(Sign_B));
  xor xor_1 (Sign_Quo, Sign_A, Sign_B);
  Divider #(.width(32)) divider_1 (.a(sign_1_out), .b(sign_2_out), .out(plus_Quo), .rem(plus_Rem));  // open: upper
  Negator #(.width(32)) negator_1 (.in(plus_Quo), .out(minus_Quo));
  Negator #(.width(32)) negator_2 (.in(plus_Rem), .out(minus_Rem));
  Multiplexer #(.width(32), .enable("false")) multiplexer_1 (
    .in0(plus_Quo), .in1(minus_Quo), .out(Low), .sel(Sign_Quo));
  Multiplexer #(.width(32), .enable("false")) multiplexer_2 (.in0(plus_Rem), .in1(minus_Rem), .out(High), .sel(Sign_A));

  // Notes on the sheet:
  //   Signed Divider
  //   Quotient Sign
  //   Negator
  //   1) Divide the operand's absolute value
  //   2) Negate the quotient if the signs of the operands are opposite
  //   3) Make the sign of the remainder match the dividend
  //   Outputs
endmodule

module SignMul (
  input  [31:0] A,
  input  [31:0] B,
  output [31:0] Low,
  output [31:0] High
);

  wire adder_1_cout, Sign_A, Sign_B, Sign_R;
  wire [31:0] minus_High, minus_Low, not_1_out, not_2_out, plus_High, plus_Low, sign_1_out, sign_2_out;

  Sign sign_1 (.In(A), .Out(sign_1_out), .Sign(Sign_A));
  Sign sign_2 (.In(B), .Out(sign_2_out), .Sign(Sign_B));
  xor xor_1 (Sign_R, Sign_A, Sign_B);
  Multiplier #(.width(32)) multiplier_1 (
    .a(sign_1_out), .b(sign_2_out), .out(plus_Low), .cout(plus_High));  // open: cin
  assign not_1_out = ~plus_Low;  // NOT_Gate not_1, 32 bits wide
  assign not_2_out = ~plus_High;  // NOT_Gate not_2, 32 bits wide
  Adder #(.width(32)) adder_1 (.a(not_1_out), .b(32'h1), .out(minus_Low), .cout(adder_1_cout));  // open: cin
  Adder #(.width(32)) adder_2 (.a(not_2_out), .b({32{1'b0}}), .out(minus_High), .cin(adder_1_cout));  // open: cout
  Multiplexer #(.width(32), .enable("false")) multiplexer_1 (.in0(plus_Low), .in1(minus_Low), .out(Low), .sel(Sign_R));
  Multiplexer #(.width(32), .enable("false")) multiplexer_2 (
    .in0(plus_High), .in1(minus_High), .out(High), .sel(Sign_R));

  // Notes on the sheet:
  //   Final Sign
  //   Signed Multiplier
  //   Negator
  //   1) Multiply the operand's absolute value
  //   2) Invert the result if neccesary according to the signs of the operands
  //   Outputs
endmodule

module ALU (
  input  [31:0] A,
  input  [31:0] B,
  input  [2:0] S,
  output [31:0] R,
  output Positive,
  output Zero,
  output Negative,
  output [31:0] Lo,
  output [31:0] Hi
);

  wire comparator_1_lt, comparator_2_lt;
  wire [31:0] And, Diff, HiDiv, HiDivu, HiMult, HiMulu, LoDiv, LoDivu, LoMult, LoMulu, Nor, Or, slt, sltu,
       Sum, Xor;

  Adder #(.width(32)) adder_1 (.a(A), .b(B), .out(Sum));  // open: cin, cout
  Subtractor #(.width(32)) subtractor_1 (.a(A), .b(B), .out(Diff));  // open: bin, bout
  assign And = A & B;  // AND_Gate and_1, 32 bits wide
  assign Or = A | B;  // OR_Gate or_1, 32 bits wide
  assign Nor = ~Or;  // NOT_Gate not_1, 32 bits wide
  assign Xor = A ^ B;  // XOR_Gate xor_1, 32 bits wide
  Multiplier #(.width(32)) multiplier_1 (.a(A), .b(B), .out(LoMulu), .cout(HiMulu));  // open: cin
  Comparator #(.width(32)) comparator_1 (.a(A), .b(B), .lt(comparator_1_lt));  // open: gt, eq
  Comparator #(.width(32), .mode("unsigned")) comparator_2 (.a(A), .b(B), .lt(comparator_2_lt));  // open: gt, eq
  Divider #(.width(32)) divider_1 (.a(A), .b(B), .out(LoDivu), .rem(HiDivu));  // open: upper
  assign slt = {{31{1'b0}}, comparator_1_lt};  // Bit_Extender bit_extender_1
  assign sltu = {{31{1'b0}}, comparator_2_lt};  // Bit_Extender bit_extender_2
  Multiplexer #(.select(3), .width(32), .enable("false")) multiplexer_1 (
    .in0(Sum), .in1(Diff), .in2(And), .in3(Or), .in4(Nor), .in5(Xor), .in6(slt), .in7(sltu), .out(R), .sel(S));
  Multiplexer #(.select(2), .width(32), .enable("false")) multiplexer_2 (
    .in0(LoMult), .in1(LoMulu), .in2(LoDiv), .in3(LoDivu), .out(Lo), .sel(S[1:0]));
  Multiplexer #(.select(2), .width(32), .enable("false")) multiplexer_3 (
    .in0(HiMult), .in1(HiMulu), .in2(HiDiv), .in3(HiDivu), .out(Hi), .sel(S[1:0]));
  Comparator #(.width(32)) comparator_3 (.a(R), .b({32{1'b0}}), .gt(Positive), .eq(Zero), .lt(Negative));

  // Other names for the same wires on the sheet: LoHi_S[1:0] = S[1:0]

  // Notes on the sheet:
  //   Inputs
  //   ALU
  //   Arithmetic Ops
  //   Logic Ops
  //   Unisgned
  //   Outputs
endmodule

module InstructionSplitter (
  input  [31:0] Inst,
  input  IM_R_W,
  input  Clk,
  input  Rst,
  output [5:0] Op,
  output [5:0] Func__Code,
  output [25:0] Destino,
  output [4:0] RS,
  output [4:0] RT,
  output [4:0] RD,
  output [31:0] Sign_Const,
  output [31:0] Unsgn_Const
);

  Register register_1 (.Data_In(Inst), .Load(IM_R_W), .Clock(Clk), .Reset(Rst), .Current_Value({Op, Destino}));
  assign Sign_Const = {{16{Destino[15]}}, Destino[15:0]};  // Bit_Extender bit_extender_1
  assign Unsgn_Const = {{16{1'b0}}, Destino[15:0]};  // Bit_Extender bit_extender_2

  assign Func__Code = Destino[5:0];
  assign RD = Destino[15:11];
  assign RS = Destino[25:21];
  assign RT = Destino[20:16];

  // Other names for the same wires on the sheet: Destin[25:0] = Destino; FC[5:0] = Destino[5:0];
  //   K[15:0] = Destino[15:0]

  // Notes on the sheet:
  //   Inputs
  //   Outputs
endmodule

module BranchControl (
  input  [31:0] PC_in,
  input  [1:0] BCSel,
  input  [2:0] FlagS,
  input  [31:0] K,
  input  [25:0] Destino,
  input  [31:0] Register,
  input  Z,
  input  N,
  input  P,
  output [31:0] PC_out
);

  wire Flag, lez, neq;
  wire [31:0] adder_1_out, adder_2_out, multiplexer_2_out, shifter_1_out;

  not not_1 (neq, Z);
  Multiplexer #(.select(3), .enable("false")) multiplexer_1 (
    .in0(Z), .in1(lez), .in2(neq), .in6(N), .in7(P), .out(Flag), .sel(FlagS));  // open: in3, in4, in5
  not not_2 (lez, P);
  Adder #(.width(32)) adder_1 (.a(PC_in), .b(32'h4), .out(adder_1_out));  // open: cin, cout
  Shifter #(.width(32)) shifter_1 (.in(K), .\dist (5'b00010), .out(shifter_1_out));
  Adder #(.width(32)) adder_2 (.a(adder_1_out), .b(shifter_1_out), .out(adder_2_out));  // open: cin, cout
  Multiplexer #(.width(32), .enable("false")) multiplexer_2 (
    .in0(adder_1_out), .in1(adder_2_out), .out(multiplexer_2_out), .sel(Flag));
  Multiplexer #(.select(2), .width(32), .enable("false")) multiplexer_3 (
    .in0(adder_1_out), .in1(multiplexer_2_out), .in2(Register), .in3({PC_in[31:28], Destino, 2'b00}),
    .out(PC_out), .sel(BCSel));

  // Other names for the same wires on the sheet: BCS[1:0] = BCSel; eq = Z; FS[2:0] = FlagS; gtz = P; ltz = N;
  //   R[31:0] = Register

  // Notes on the sheet:
  //   Direccion de la
  //   Instruccion Actual
  //   Branch Control
  //   Direccion de la
  //   Proxima Instruccion
endmodule

module ControlUnit_2 (
  input  [5:0] in_1,
  input  [5:0] in_2,
  input  in_3,
  input  in_4,
  input  in_5,
  output out_6,
  output [2:0] out_7,
  output out_8,
  output [2:0] out_9,
  output out_10,
  output [1:0] out_11,
  output out_12,
  output out_13,
  output out_14,
  output out_15,
  output [1:0] out_16,
  output out_17,
  output [2:0] out_18,
  output out_19,
  output out_20,
  output [1:0] out_21,
  output out_22,
  output out_23,
  output out_24
);

  wire add, addi, \and , andi, beq, bgtz, blez, bltz, bne, d_ff_1_q, d_ff_2_q, demultiplexer_1_out0,
       demultiplexer_1_out1, demultiplexer_2_out0, div, divu, En_AL, En_B, En_I, En_S, En_Sp, En_W, EndS,
       Endw, haltl, jmp, jr, kbd_t, Load_IM_q, lw, mfhi, mflo, mul, mulu, next, nop, \nor , not_1_out, \or ,
       or_2_out, or_6_out, ori, PCal, PCb, PCi, PCs, PCsp, PCw, pop, push, RamWs, RamWw, RFal, RfE, RFi, Rfs,
       Rfw, rnd, S_DAi, S_DAw, slt, slti, sltiu, sltu, StartRamF, StartRams, StartRamw, sub, sw, tty_t,
       Type_AL, Type_B, Type_I, Type_S, Type_Sp, Type_W, \xor , xori;
  wire [1:0] S_Adrs, S_Adrw, S_BCal, S_BCb, S_Bi, S_Bs, S_Bw;
  wire [2:0] S_ALUal, S_ALUb, S_ALUi, S_ALUs, S_Dial, S_DiE, S_Dis, S_Diw;

  InstructionDecoder instructiondecoder_1 (
    .OpCode(in_1), .FunCode(in_2), .addi(addi), .beq(beq), .slti(slti), .add(add), .\and (\and ), .nop(nop),
    .andi(andi), .bne(bne), .sltiu(sltiu), .sub(sub), .\or (\or ), .push(push), .ori(ori), .blez(blez),
    .lw(lw), .pop(pop), .mul(mul), .\nor (\nor ), .xori(xori), .bgtz(bgtz), .sw(sw), .tty(tty_t),
    .mulu(mulu), .\xor (\xor ), .jmp(jmp), .bltz(bltz), .div(div), .mfhi(mfhi), .halt(haltl), .mflo(mflo),
    .divu(divu), .rnd(rnd), .slt(slt), .jr(jr), .kbd(kbd_t), .sltu(sltu));
  D_Flip_Flop d_ff_1 (.clk(in_3), .D(demultiplexer_1_out0), .Q(d_ff_1_q), .preset(in_4));  // open: Qn, en, reset
  Demultiplexer #(.enable("false")) demultiplexer_1 (
    .out0(demultiplexer_1_out0), .out1(demultiplexer_1_out1), .in(d_ff_1_q), .sel(not_1_out));
  not not_1 (not_1_out, in_4);
  or or_1 (StartRamF, next, demultiplexer_1_out1);
  D_Flip_Flop d_ff_2 (.clk(in_3), .D(demultiplexer_2_out0), .Q(d_ff_2_q));  // open: Qn, preset, en, reset
  or or_2 (or_2_out, StartRamF, d_ff_2_q);
  Demultiplexer #(.enable("false")) demultiplexer_2 (
    .out0(demultiplexer_2_out0), .out1(out_12), .in(or_2_out), .sel(in_5));
  TYPE_AL type_al_1 (
    .in_1(En_AL), .in_2(add), .in_3(sub), .in_4(\and ), .in_5(\or ), .in_6(\xor ), .in_7(\nor ), .in_8(slt),
    .in_9(sltu), .in_10(mul), .in_11(mulu), .in_12(div), .in_13(divu), .in_14(mfhi), .in_15(mflo),
    .in_16(jr), .in_17(nop), .out_19(RFal), .out_20(S_ALUal), .out_23(S_BCal), .out_21(out_6),
    .out_22(S_Dial), .out_18(PCal));
  D_Flip_Flop Load_IM (.clk(in_3), .D(out_12), .Q(Load_IM_q));  // open: Qn, preset, en, reset
  and and_1 (En_AL, Type_AL, Load_IM_q);
  and and_2 (En_I, Type_I, Load_IM_q);
  and and_3 (En_B, Type_B, Load_IM_q);
  and and_4 (En_W, Type_W, Load_IM_q);
  and and_5 (En_Sp, Type_Sp, Load_IM_q);
  and and_6 (En_S, Type_S, Load_IM_q);
  TYPE_WORD type_word_1 (
    .in_1(En_W), .in_2(in_3), .in_3(lw), .in_4(in_5), .in_5(sw), .out_13(S_Diw), .out_8(Endw),
    .out_9(StartRamw), .out_10(S_Bw), .out_12(S_Adrw), .out_14(PCw), .out_11(RamWw), .out_6(Rfw),
    .out_7(S_DAw));
  TYPE_STACK type_stack_1 (
    .in_1(pop), .in_2(push), .in_3(En_S), .in_4(in_5), .in_5(in_3), .out_11(out_13), .out_14(S_Bs),
    .out_17(out_23), .out_9(S_Adrs), .out_12(PCs), .out_16(S_ALUs), .out_10(StartRams), .out_15(S_Dis),
    .out_13(EndS), .out_6(Rfs), .out_7(RamWs), .out_8(out_14));
  or or_3 (next, En_AL, En_I, En_Sp, En_B, Endw, EndS);
  TYPE_INM type_inm_1 (
    .in_1(En_I), .in_2(addi), .in_3(andi), .in_4(ori), .in_5(xori), .in_6(slti), .in_7(sltiu),
    .out_10(S_DAi), .out_11(PCi), .out_12(RFi), .out_9(S_Bi), .out_8(S_ALUi));
  TYPE_BRANCH type_branch_1 (
    .in_1(En_B), .in_2(beq), .in_3(bne), .in_4(blez), .in_5(bgtz), .in_6(bltz), .in_7(jmp), .out_8(PCb),
    .out_11(out_18), .out_9(S_ALUb), .out_10(S_BCb));
  or or_4 (Type_B, beq, bne, blez, bgtz, bltz, jmp);
  or or_5 (Type_AL, add, sub, \and , \or , \xor , \nor , slt, sltu, mul, mulu, div, divu, mfhi, mflo, jr, nop);
  or or_6 (or_6_out, haltl, out_24);
  D_Flip_Flop #(.trigger("high")) Halt (.clk(in_3), .D(or_6_out), .Q(out_24));  // open: Qn, preset, en, reset
  or or_7 (Type_Sp, kbd_t, rnd, tty_t);
  or or_8 (Type_W, lw, sw);
  or or_9 (Type_S, pop, push);
  or or_10 (Type_I, addi, andi, ori, xori, slti, sltiu);
  TYPE_SPECIAL type_special_1 (
    .in_1(En_Sp), .in_2(kbd_t), .in_3(rnd), .in_4(tty_t), .out_7(out_17), .out_5(RfE), .out_6(S_DiE),
    .out_8(PCsp), .out_9(out_22));
  assign out_7 = S_ALUal | S_ALUi | S_ALUb | S_ALUs;  // OR_Gate or_11, 3 bits wide
  assign out_16 = S_Bs | S_Bi | S_Bw;  // OR_Gate or_12, 2 bits wide
  assign out_21 = S_BCb | S_BCal;  // OR_Gate or_13, 2 bits wide
  assign out_9 = S_Dial | S_Dis | S_Diw | S_DiE;  // OR_Gate or_14, 3 bits wide
  assign out_11 = S_Adrs | S_Adrw;  // OR_Gate or_15, 2 bits wide
  or or_16 (out_20, S_DAi, S_DAw);
  or or_17 (out_10, RamWs, RamWw);
  or or_18 (out_19, StartRams, StartRamF, StartRamw);
  or or_19 (out_8, RfE, RFal, RFi, Rfw, Rfs);
  or or_20 (out_15, PCal, PCi, PCs, PCsp, PCb, PCw);

  // Other names for the same wires on the sheet: Clk = in_3; FunCode[5:0] = in_2; HALT = out_24; En_KBD = out_22;
  //   KBD = out_22; L_IM = out_12; L_LoHi = out_6; LH = out_6; OpCode[5:0] = in_1; PC = out_15; RamReady = in_5;
  //   RamW = out_10; Rf_Rw = out_8; S_Adr[1:0] = out_11; S_ALU[2:0] = out_7; S_A = out_13; S_As = out_13;
  //   S_B[1:0] = out_16; S_BC[1:0] = out_21; S_DA = out_20; S_Di[2:0] = out_9; S_DO = out_14; S_flag[2:0] = out_18;
  //   S_flags[2:0] = out_18; SP = out_23; SPs = out_23; start = in_4; StartRam = out_19; TTY = out_17;
  //   tty_En = out_17

  // Notes on the sheet:
  //   Inputs
  //   Decoders
  //   IDLE
  //   General Circuit
  //   FETCH
  //   SWITCH
  //   Group Circuits
  //   End/Next
  //   Groups
  //   Selectors
  //   Loads
endmodule

module InstructionDecoder (
  input  [5:0] OpCode,
  input  [5:0] FunCode,
  output addi,
  output beq,
  output slti,
  output add,
  output \and ,
  output nop,
  output andi,
  output bne,
  output sltiu,
  output sub,
  output \or ,
  output push,
  output ori,
  output blez,
  output lw,
  output pop,
  output mul,
  output \nor ,
  output xori,
  output bgtz,
  output sw,
  output tty,
  output mulu,
  output \xor ,
  output jmp,
  output bltz,
  output div,
  output mfhi,
  output halt,
  output mflo,
  output divu,
  output rnd,
  output slt,
  output jr,
  output kbd,
  output sltu
);

  wire and_18_out, and_19_out, and_20_out, and_21_out, and_22_out, and_23_out, and_24_out, and_25_out,
       and_34_out, and_35_out, and_36_out, and_37_out, and_38_out, and_39_out, and_40_out, and_48_out,
       and_49_out, and_50_out, and_51_out, and_52_out, and_53_out, and_54_out, special, stack, Tipo_R;

  and and_1 (addi, ~OpCode[0], ~OpCode[1], ~OpCode[2], OpCode[3], ~OpCode[4], ~OpCode[5]);  // AND_Gate
  and and_2 (andi, ~OpCode[0], ~OpCode[1], OpCode[2], OpCode[3], ~OpCode[4], ~OpCode[5]);  // AND_Gate
  and and_3 (ori, OpCode[0], ~OpCode[1], OpCode[2], OpCode[3], ~OpCode[4], ~OpCode[5]);  // AND_Gate
  and and_4 (xori, ~OpCode[0], OpCode[1], OpCode[2], OpCode[3], ~OpCode[4], ~OpCode[5]);  // AND_Gate
  and and_5 (jmp, ~OpCode[0], OpCode[1], ~OpCode[2], ~OpCode[3], ~OpCode[4], ~OpCode[5]);  // AND_Gate
  and and_6 (Tipo_R, ~OpCode[0], ~OpCode[1], ~OpCode[2], ~OpCode[3], ~OpCode[4], ~OpCode[5]);  // AND_Gate
  and and_7 (beq, ~OpCode[0], ~OpCode[1], OpCode[2], ~OpCode[3], ~OpCode[4], ~OpCode[5]);  // AND_Gate
  and and_8 (bne, OpCode[0], ~OpCode[1], OpCode[2], ~OpCode[3], ~OpCode[4], ~OpCode[5]);  // AND_Gate
  and and_9 (blez, ~OpCode[0], OpCode[1], OpCode[2], ~OpCode[3], ~OpCode[4], ~OpCode[5]);  // AND_Gate
  and and_10 (bgtz, OpCode[0], OpCode[1], OpCode[2], ~OpCode[3], ~OpCode[4], ~OpCode[5]);  // AND_Gate
  and and_11 (bltz, OpCode[0], ~OpCode[1], ~OpCode[2], ~OpCode[3], ~OpCode[4], ~OpCode[5]);  // AND_Gate
  and and_12 (stack, ~OpCode[0], ~OpCode[1], ~OpCode[2], OpCode[3], OpCode[4], OpCode[5]);  // AND_Gate
  and and_13 (slti, ~OpCode[0], OpCode[1], ~OpCode[2], OpCode[3], ~OpCode[4], ~OpCode[5]);  // AND_Gate
  and and_14 (lw, OpCode[0], OpCode[1], ~OpCode[2], ~OpCode[3], ~OpCode[4], OpCode[5]);  // AND_Gate
  and and_15 (sw, OpCode[0], OpCode[1], ~OpCode[2], OpCode[3], ~OpCode[4], OpCode[5]);  // AND_Gate
  and and_16 (special, OpCode[0], OpCode[1], OpCode[2], OpCode[3], OpCode[4], OpCode[5]);
  and and_17 (sltiu, OpCode[0], OpCode[1], ~OpCode[2], OpCode[3], ~OpCode[4], ~OpCode[5]);  // AND_Gate
  and and_18 (and_18_out, ~FunCode[0], ~FunCode[1], ~FunCode[2], ~FunCode[3], ~FunCode[4], FunCode[5]);  // AND_Gate
  and and_19 (and_19_out, ~FunCode[0], FunCode[1], ~FunCode[2], ~FunCode[3], ~FunCode[4], FunCode[5]);  // AND_Gate
  and and_20 (and_20_out, ~FunCode[0], ~FunCode[1], ~FunCode[2], FunCode[3], FunCode[4], ~FunCode[5]);  // AND_Gate
  and and_21 (and_21_out, FunCode[0], ~FunCode[1], ~FunCode[2], FunCode[3], FunCode[4], ~FunCode[5]);  // AND_Gate
  and and_22 (and_22_out, ~FunCode[0], FunCode[1], ~FunCode[2], FunCode[3], FunCode[4], ~FunCode[5]);  // AND_Gate
  and and_23 (and_23_out, FunCode[0], FunCode[1], ~FunCode[2], FunCode[3], FunCode[4], ~FunCode[5]);  // AND_Gate
  and and_24 (and_24_out, ~FunCode[0], FunCode[1], ~FunCode[2], FunCode[3], ~FunCode[4], FunCode[5]);  // AND_Gate
  and and_25 (and_25_out, FunCode[0], FunCode[1], ~FunCode[2], FunCode[3], ~FunCode[4], FunCode[5]);  // AND_Gate
  and and_26 (add, and_18_out, Tipo_R);
  and and_27 (sub, and_19_out, Tipo_R);
  and and_28 (mul, and_20_out, Tipo_R);
  and and_29 (mulu, and_21_out, Tipo_R);
  and and_30 (div, and_22_out, Tipo_R);
  and and_31 (divu, and_23_out, Tipo_R);
  and and_32 (slt, and_24_out, Tipo_R);
  and and_33 (sltu, and_25_out, Tipo_R);
  and and_34 (and_34_out, ~FunCode[0], ~FunCode[1], FunCode[2], ~FunCode[3], ~FunCode[4], FunCode[5]);  // AND_Gate
  and and_35 (and_35_out, FunCode[0], ~FunCode[1], FunCode[2], ~FunCode[3], ~FunCode[4], FunCode[5]);  // AND_Gate
  and and_36 (and_36_out, FunCode[0], FunCode[1], FunCode[2], ~FunCode[3], ~FunCode[4], FunCode[5]);  // AND_Gate
  and and_37 (and_37_out, ~FunCode[0], ~FunCode[1], ~FunCode[2], FunCode[3], ~FunCode[4], FunCode[5]);  // AND_Gate
  and and_38 (and_38_out, ~FunCode[0], ~FunCode[1], ~FunCode[2], ~FunCode[3], FunCode[4], ~FunCode[5]);  // AND_Gate
  and and_39 (and_39_out, ~FunCode[0], FunCode[1], ~FunCode[2], ~FunCode[3], FunCode[4], ~FunCode[5]);  // AND_Gate
  and and_40 (and_40_out, ~FunCode[0], ~FunCode[1], ~FunCode[2], FunCode[3], ~FunCode[4], ~FunCode[5]);  // AND_Gate
  and and_41 (\and , and_34_out, Tipo_R);
  and and_42 (\or , and_35_out, Tipo_R);
  and and_43 (\nor , and_36_out, Tipo_R);
  and and_44 (\xor , and_37_out, Tipo_R);
  and and_45 (mfhi, and_38_out, Tipo_R);
  and and_46 (mflo, and_39_out, Tipo_R);
  and and_47 (jr, and_40_out, Tipo_R);
  and and_48 (and_48_out, ~FunCode[0], ~FunCode[1], ~FunCode[2], ~FunCode[3], ~FunCode[4], ~FunCode[5]);  // AND_Gate
  and and_49 (and_49_out, FunCode[0], ~FunCode[1], ~FunCode[2], ~FunCode[3], ~FunCode[4], ~FunCode[5]);  // AND_Gate
  and and_50 (and_50_out, ~FunCode[0], ~FunCode[1], ~FunCode[2], ~FunCode[3], ~FunCode[4], ~FunCode[5]);  // AND_Gate
  and and_51 (and_51_out, FunCode[0], ~FunCode[1], ~FunCode[2], ~FunCode[3], ~FunCode[4], ~FunCode[5]);  // AND_Gate
  and and_52 (and_52_out, FunCode[0], FunCode[1], FunCode[2], FunCode[3], FunCode[4], FunCode[5]);
  and and_53 (and_53_out, ~FunCode[0], FunCode[1], ~FunCode[2], ~FunCode[3], ~FunCode[4], ~FunCode[5]);  // AND_Gate
  and and_54 (and_54_out, ~FunCode[0], ~FunCode[1], FunCode[2], ~FunCode[3], ~FunCode[4], ~FunCode[5]);  // AND_Gate
  and and_55 (nop, and_48_out, Tipo_R);
  and and_56 (push, and_49_out, stack);
  and and_57 (pop, and_50_out, stack);
  and and_58 (tty, and_51_out, special);
  and and_59 (halt, and_52_out, special);
  and and_60 (rnd, and_53_out, special);
  and and_61 (kbd, and_54_out, special);

  // Other names for the same wires on the sheet: f0 = FunCode[0]; f1 = FunCode[1]; f2 = FunCode[2]; f3 = FunCode[3];
  //   f4 = FunCode[4]; f5 = FunCode[5]; o0 = OpCode[0]; o1 = OpCode[1]; o2 = OpCode[2]; o3 = OpCode[3];
  //   o4 = OpCode[4]; o5 = OpCode[5]

  // Notes on the sheet:
  //   OP CODE
  //   GROUP
  //   FUNC CODE
endmodule

module TYPE_AL (
  input  in_1,
  input  in_2,
  input  in_3,
  input  in_4,
  input  in_5,
  input  in_6,
  input  in_7,
  input  in_8,
  input  in_9,
  input  in_10,
  input  in_11,
  input  in_12,
  input  in_13,
  input  in_14,
  input  in_15,
  input  in_16,
  input  in_17,
  output out_18,
  output out_19,
  output [2:0] out_20,
  output out_21,
  output [2:0] out_22,
  output [1:0] out_23
);

  wire not_1_out, or_5_out, or_6_out, or_7_out, or_8_out;
  wire [1:0] or_1_out;
  wire [2:0] or_2_out;

  not not_1 (not_1_out, in_14);
  or or_1 (or_1_out[0], in_15, in_14);
  or or_2 (or_2_out[0], in_6, in_3, in_5, in_11, in_9, in_13);
  or or_3 (or_2_out[1], in_13, in_4, in_5, in_8, in_9, in_12);
  or or_4 (or_2_out[2], in_7, in_8, in_6, in_9);
  or or_5 (or_5_out, in_10, in_11, in_12, in_13);
  and and_1 (out_21, or_5_out, in_1);
  and and_2 (or_1_out[1], in_15, not_1_out);
  assign out_23 = {in_16, 1'b0} & {2{in_1}};  // AND_Gate and_3, 2 bits wide
  or or_6 (or_6_out, or_2_out[0], or_2_out[1], or_2_out[2]);
  or or_7 (or_7_out, in_2, or_6_out);
  assign out_20 = or_2_out & {3{in_1}};  // AND_Gate and_4, 3 bits wide
  assign out_22 = {in_14, or_1_out} & {3{in_1}};  // AND_Gate and_5, 3 bits wide
  or or_8 (or_8_out, or_7_out, in_14, in_15);
  and and_6 (out_19, or_8_out, ~in_11, ~in_12, ~in_13, in_1);  // AND_Gate

  assign out_18 = in_1;

  // Other names for the same wires on the sheet: jr = in_16; mfhi = in_14; EN = in_1; PC = in_1; add = in_2;
  //   and = in_4; div = in_12; divu = in_13; LH = out_21; mflo = in_15; mul = in_10; mulu = in_11; nop = in_17;
  //   nor = in_7; or = in_5; Rf_Rw = out_19; S_ALU[2:0] = out_20; S_BC[1:0] = out_23; S_Di[2:0] = out_22; slt = in_8;
  //   sltu = in_9; sub = in_3; xor = in_6
endmodule

module TYPE_INM (
  input  in_1,
  input  in_2,
  input  in_3,
  input  in_4,
  input  in_5,
  input  in_6,
  input  in_7,
  output [2:0] out_8,
  output [1:0] out_9,
  output out_10,
  output out_11,
  output out_12
);

  wire or_2_out, or_3_out;
  wire [0:0] or_1_out;
  wire [2:0] or_5_out;

  or or_1 (or_1_out[0], in_2, in_3, in_4, in_5, in_6, in_7);
  and and_1 (out_10, or_1_out[0], in_1);
  assign out_9 = {1'b0, or_1_out[0]} & {2{in_1}};  // AND_Gate and_2, 2 bits wide
  or or_2 (or_2_out, in_4, in_7);
  or or_3 (or_3_out, in_6, in_3);
  or or_4 (or_5_out[2], in_7, in_6, in_5);
  or or_5 (or_5_out[0], in_5, or_2_out);
  or or_6 (or_5_out[1], or_2_out, or_3_out);
  assign out_8 = or_5_out & {3{in_1}};  // AND_Gate and_3, 3 bits wide

  assign out_11 = in_1;
  assign out_12 = in_1;

  // Other names for the same wires on the sheet: En = in_1; PC = in_1; RW_RF = in_1; addi = in_2; andi = in_3;
  //   ori = in_4; S_ALU[2:0] = out_8; S_B[1:0] = out_9; S_DA = out_10; slti = in_6; sltiu = in_7; xori = in_5
endmodule

module TYPE_BRANCH (
  input  in_1,
  input  in_2,
  input  in_3,
  input  in_4,
  input  in_5,
  input  in_6,
  input  in_7,
  output out_8,
  output [2:0] out_9,
  output [1:0] out_10,
  output [2:0] out_11
);

  wire [0:0] or_1_out, or_4_out;
  wire [2:0] or_3_out;

  or or_1 (or_1_out[0], in_2, in_3, in_4, in_5, in_6);
  or or_2 (or_3_out[2], in_6, in_5);
  nor nor_1 (or_3_out[1], in_2, in_4);
  or or_3 (or_3_out[0], in_4, in_5);
  or or_4 (or_4_out[0], or_1_out[0], in_7);
  assign out_10 = {in_7, or_4_out[0]} & {2{in_1}};  // AND_Gate and_1, 2 bits wide
  assign out_11 = or_3_out & {3{in_1}};  // AND_Gate and_2, 3 bits wide
  assign out_9 = {2'b00, or_1_out[0]} & {3{in_1}};  // AND_Gate and_3, 3 bits wide

  assign out_8 = in_1;

  // Other names for the same wires on the sheet: jmp = in_7; EN = in_1; PC = in_1; beq = in_2; bgtz = in_5;
  //   blez = in_4; bltz = in_6; bne = in_3; S_ALU[2:0] = out_9; S_BC[1:0] = out_10; S_flags[2:0] = out_11
endmodule

module TYPE_WORD (
  input  in_1,
  input  in_2,
  input  in_3,
  input  in_4,
  input  in_5,
  output out_6,
  output out_7,
  output out_8,
  output out_9,
  output [1:0] out_10,
  output out_11,
  output [1:0] out_12,
  output [2:0] out_13,
  output out_14
);

  wire d_ff_1_q, d_ff_2_q, demultiplexer_1_out0, demultiplexer_2_out0, EndLW, EndSW, PCs, S_Adr0l, startRaml,
       startRams;

  and and_1 (startRaml, in_1, in_3);
  D_Flip_Flop d_ff_1 (.clk(in_2), .D(demultiplexer_1_out0), .Q(d_ff_1_q));  // open: Qn, preset, en, reset
  and and_2 (startRams, in_1, in_5);
  D_Flip_Flop d_ff_2 (.clk(in_2), .D(demultiplexer_2_out0), .Q(d_ff_2_q));  // open: Qn, preset, en, reset
  or or_1 (S_Adr0l, startRaml, d_ff_1_q);
  or or_2 (out_11, startRams, d_ff_2_q);
  Demultiplexer #(.enable("false")) demultiplexer_1 (
    .out0(demultiplexer_1_out0), .out1(out_6), .in(S_Adr0l), .sel(in_4));
  Demultiplexer #(.enable("false")) demultiplexer_2 (.out0(demultiplexer_2_out0), .out1(PCs), .in(out_11), .sel(in_4));
  D_Flip_Flop d_ff_3 (.clk(in_2), .D(PCs), .Q(EndSW));  // open: Qn, preset, en, reset
  D_Flip_Flop d_ff_4 (.clk(in_2), .D(out_6), .Q(EndLW));  // open: Qn, preset, en, reset
  or or_3 (out_8, EndLW, EndSW);
  or or_4 (out_9, startRaml, startRams);
  or or_5 (out_10[0], out_11, S_Adr0l);
  or or_6 (out_12[0], S_Adr0l, out_11);
  or or_7 (out_14, out_6, PCs);

  assign out_7 = out_6;
  assign out_10[1] = 1'b0;
  assign out_12[1] = 1'b0;
  assign out_13 = {2'b00, out_6};

  // Other names for the same wires on the sheet: Clk = in_2; EN = in_1; ENDw = out_8; LoadWord = in_3; PC = out_14;
  //   RamReady = in_4; S_Adr[0] = out_12[0]; S_B[0] = out_10[0]; S_B0l = S_Adr0l; RamW = out_11; S_Adr0s = out_11;
  //   S_B0s = out_11; PCl = out_6; Rf_Rw = out_6; S_DA = out_6; S_Di[0] = out_6; S_Di0 = out_6; startRam = out_9;
  //   StoreWord = in_5

  // Notes on the sheet:
  //   LOAD
  //   STORE
endmodule

module TYPE_SPECIAL (
  input  in_1,
  input  in_2,
  input  in_3,
  input  in_4,
  output out_5,
  output [2:0] out_6,
  output out_7,
  output out_8,
  output out_9
);

  wire [2:2] or_1_out;

  or or_1 (or_1_out[2], in_2, in_3);
  and and_1 (out_5, or_1_out[2], in_1);
  and and_2 (out_7, in_4, in_1);
  assign out_6 = {{2{or_1_out[2]}}, in_2} & {3{in_1}};  // AND_Gate and_3, 3 bits wide
  and and_4 (out_9, in_2, in_1);

  assign out_8 = in_1;

  // Other names for the same wires on the sheet: kbd = in_2; En = in_1; PC = in_1; kbdEn = out_9; Rf = out_5;
  //   rnd = in_3; S_Di[2:0] = out_6; tty = in_4; tty_Enable = out_7
endmodule

module TYPE_STACK (
  input  in_1,
  input  in_2,
  input  in_3,
  input  in_4,
  input  in_5,
  output out_6,
  output out_7,
  output out_8,
  output [1:0] out_9,
  output out_10,
  output out_11,
  output out_12,
  output out_13,
  output [1:0] out_14,
  output [2:0] out_15,
  output [2:0] out_16,
  output out_17
);

  wire d_ff_1_q, d_ff_3_q, demultiplexer_1_out0, demultiplexer_2_out0, EndPop, EndPush, PCpush, S_Adr1pop,
       startRampop, startRampush;

  or or_1 (out_11, out_6, out_16[0]);
  or or_2 (out_14[1], out_6, out_16[0]);
  and and_1 (startRampop, in_3, in_1);
  D_Flip_Flop d_ff_1 (.clk(in_5), .D(demultiplexer_1_out0), .Q(d_ff_1_q));  // open: Qn, preset, en, reset
  and and_2 (out_16[0], in_3, in_2);
  or or_3 (S_Adr1pop, startRampop, d_ff_1_q);
  or or_4 (out_9[1], S_Adr1pop, out_7);
  or or_5 (out_17, out_6, out_16[0]);
  Demultiplexer #(.enable("false")) demultiplexer_1 (
    .out0(demultiplexer_1_out0), .out1(out_6), .in(S_Adr1pop), .sel(in_4));
  D_Flip_Flop d_ff_2 (.clk(in_5), .D(out_16[0]), .Q(startRampush));  // open: Qn, preset, en, reset
  D_Flip_Flop d_ff_3 (.clk(in_5), .D(demultiplexer_2_out0), .Q(d_ff_3_q));  // open: Qn, preset, en, reset
  or or_6 (out_12, out_6, PCpush);
  or or_7 (out_7, startRampush, d_ff_3_q);
  or or_8 (out_10, startRampop, startRampush);
  D_Flip_Flop d_ff_4 (.clk(in_5), .D(out_6), .Q(EndPop));  // open: Qn, preset, en, reset
  Demultiplexer #(.enable("false")) demultiplexer_2 (
    .out0(demultiplexer_2_out0), .out1(PCpush), .in(out_7), .sel(in_4));
  or or_9 (out_13, EndPop, EndPush);
  D_Flip_Flop d_ff_5 (.clk(in_5), .D(PCpush), .Q(EndPush));  // open: Qn, preset, en, reset

  assign out_8 = out_7;
  assign out_9[0] = 1'b0;
  assign out_14[0] = out_14[1];
  assign out_15 = {2'b00, out_6};
  assign out_16[2:1] = 2'b00;

  // Other names for the same wires on the sheet: Clk = in_5; En = in_3; ENDStack = out_13; PC = out_12; pop = in_1;
  //   push = in_2; RamReady = in_4; S_A = out_11; S_Adr[1] = out_9[1]; S_ALU[0] = out_16[0]; S_ALU0 = out_16[0];
  //   S_Apush = out_16[0]; S_Bpush = out_16[0]; SP_RWpush = out_16[0]; S_B[1:0] = {2{out_14[1]}}; PCpop = out_6;
  //   Rf_Rw = out_6; S_Apop = out_6; S_Bpop = out_6; S_Di[0] = out_6; S_Di0 = out_6; SP_RWpop = out_6; RamW = out_7;
  //   S_Adr1push = out_7; S_Do = out_7; SP_RW = out_17; startRam = out_10

  // Notes on the sheet:
  //   POP
  //   PUSH
endmodule

module RamHandler (
  input  [31:0] Addres_In,
  input  [31:0] Ram_out_0,
  input  [31:0] Ram_out_1,
  input  [31:0] Ram_out_2,
  input  [31:0] Ram_out_3,
  input  [3:0] Read_Time,
  input  Clk,
  input  Rst,
  input  [3:0] Write_Time,
  input  Start,
  input  R_W,
  output [31:0] From_RAM,
  output [3:0] Mask,
  output [15:0] ADDR,
  output [1:0] Bank,
  output RAMReady,
  output Chip_Select,
  output RAM_Write
);

  wire Clear, comparator_1_lt, demultiplexer_1_out0, IsFetch, or_2_out, Wait_q;
  wire [3:0] counter_1_q, Time;
  wire [31:0] multiplexer_2_out;

  Multiplexer #(.width(4), .enable("false")) multiplexer_1 (.in0(Read_Time), .in1(Write_Time), .out(Time), .sel(R_W));
  D_Flip_Flop Wait (.clk(Clk), .D(demultiplexer_1_out0), .Q(Wait_q));  // open: Qn, preset, en, reset
  or or_1 (Chip_Select, Wait_q, Start);
  Counter #(.width(4), .max('hf)) counter_1 (
    .count(Chip_Select), .Q(counter_1_q), .clk(Clk), .clr(or_2_out));  // open: load, D, carry
  or or_2 (or_2_out, Rst, Clear);
  Demultiplexer #(.enable("false")) demultiplexer_1 (
    .out0(demultiplexer_1_out0), .out1(RAMReady), .in(Chip_Select), .sel(IsFetch));
  Comparator #(.width(4), .mode("unsigned")) comparator_1 (
    .a(counter_1_q), .b(Time), .lt(comparator_1_lt));  // open: gt, eq
  not not_1 (IsFetch, comparator_1_lt);
  D_Flip_Flop End (.clk(Clk), .D(RAMReady), .Q(Clear));  // open: Qn, preset, en, reset
  Multiplexer #(.select(2), .width(32), .enable("false")) multiplexer_2 (
    .in0(Ram_out_0), .in1(Ram_out_1), .in2(Ram_out_2), .in3(Ram_out_3), .out(multiplexer_2_out),
    .sel(Addres_In[3:2]));
  Decoder #(.select(2), .enable("false")) decoder_1 (
    .out0(Mask[0]), .out1(Mask[1]), .out2(Mask[2]), .out3(Mask[3]), .sel(Addres_In[3:2]));
  SwapLittleEndian swaplittleendian_1 (.Input(multiplexer_2_out), .Output(From_RAM));
  and and_1 (RAM_Write, R_W, Chip_Select);

  assign ADDR = Addres_In[19:4];
  assign Bank = Addres_In[3:2];

  // Other names for the same wires on the sheet: Block[15:0] = Addres_In[19:4]; End = RAMReady; Count = Chip_Select;
  //   CS = Chip_Select; RAM_Wr = Chip_Select; RW = R_W

  // Notes on the sheet:
  //   ADDRESS
  //   DATA FROM RAM
  //   RAM TIMING
  //   CONTROL SIGNALS
  //   TIMER
  //   FLOW CONTROL
endmodule

module SwapLittleEndian (
  input  [31:0] Input,
  output [31:0] Output
);


  assign Output = {Input[7:0], Input[15:8], Input[23:16], Input[31:24]};
endmodule
